# Fritzing sketch RFIDDoorACS_Fritzing_Circuit (saved by Fritzing 0.9.2b)
breadboards: 1

parts:
  U1 = RELAY [package=relay-g5q]
  Q1 = NPN-Transistor [package="TO92 [THT]"]
  R1 = Resistor [tolerance=±5% resistance=1M package=THT]
  U2 = 555 Timer [package="DIP8 [THT]"]
  R2 = Rotary Potentiometer (Small) [maximum_resistance=100kΩ package=THT]
  680uF = Capacitor Polarized [package=panasonic_g]
  C1 = Ceramic Capacitor [capacitance=10nF package="200 mil [THT, multilayer]"]
  IC1 = IC, DIP package, 14 pins [chip_label=NTE40107B]
  R3 = Resistor [tolerance=±5% resistance=1k package=THT]
  IC2 = IC, DIP package, 14 pins [chip_label=NTE4071B]
  R4 = Resistor [tolerance=±5% resistance=1k package=THT]
  R5 = Resistor [tolerance=±5% resistance=1k package=THT]
  R6 = Resistor [tolerance=±5% resistance=1k package=THT]
  Part1 = Intel Edison Arduinobreakout
  J1 = screw terminal, 3 pins
  J2 = screw terminal, 3 pins
  Grove3 = Grove OLED 128x96
  RFID1 = Parallax RFID Reader Module

nets:
  VCC: U1.COIL2, U2.Pin_8, R2.leg1, IC1.pin14, IC2.pin14, Part1.5V, Grove3.VCC, RFID1.VCC
  N1: U1.MAIN, J2.pin3
  N2: U1.NO, J2.pin2
  N3: U1.NC, J2.pin1
  N4: U1.COIL1, Q1.C
  GND: Q1.E, R1.Pin_1, U2.Pin_1, U2.Pin_4, 680uF.-, C1.1, IC1.pin7, R3.Pin_1, IC2.pin7, R4.Pin_1, R5.Pin_1, R6.Pin_1, Part1.GND, J1.pin1, Grove3.GND, RFID1.GND
  N5: Q1.B, R1.Pin_0, U2.Pin_3
  N6: U2.Pin_2, IC1.pin3, R3.Pin_0
  N7: U2.Pin_5, C1.0
  N8: U2.Pin_6, U2.Pin_7, R2.wiper, 680uF.+
  N9: IC1.pin1, R5.Pin_0, Part1.D8
  N10: IC1.pin2, IC2.pin3
  N11: IC2.pin1, R4.Pin_0, Part1.D12/MISO
  N12: IC2.pin2, R6.Pin_0, J1.pin2
  N13: Part1.A4/SDA, Grove3.SDA
  N14: Part1.A5/SCL, Grove3.SCL
  N15: Part1.D0/RX, RFID1.Sout
  N16: Part1.D1/TX, RFID1./ENABLE
